# Fritzing sketch circuit laytou (saved by Fritzing 0.9.3b)

parts:
  Part1 = Arduino Uno (Rev3)
  part = Resistor [tolerance=±5% resistance=2.2k package=THT]
  part_2 = Resistor [tolerance=±5% resistance=68 package=THT]
  part_3 = Resistor [tolerance=±5% resistance=68 package=THT]
  CONN1 = USB connector [package=THT]
  part_4 = Zener Diode [part_number=1N4732A breakdown_voltage=3.6V package="300 mil [THT]"]
  part_5 = Zener Diode [part_number=1N4732A breakdown_voltage=3.6V package="300 mil [THT]"]

nets:
  N1: Part1.D2, part_3.Pin_0
  N2: Part1.D3_PWM, part_2.Pin_0
  N3: Part1.GND, CONN1.chassis6, part_4.anode, part_5.anode
  VIN: Part1.VIN, part.Pin_1, CONN1.5V
  N4: part.Pin_0, part_3.Pin_1, CONN1.d-, part_4.cathode
  N5: part_2.Pin_1, CONN1.d+, part_5.cathode
